# Fritzing sketch AutonomousGrabberCircuit (saved by Fritzing 0.9.2b)

parts:
  Part1 = Arduino Mega 2560 (Rev3)  # not connected
  S2 = Momentary Switch [package=tactile-pth]  # not connected
  S3 = Momentary Switch [package=tactile-pth]  # not connected
  S4 = Momentary Switch [package=tactile-pth]  # not connected
  S5 = Momentary Switch [package=tactile-pth]  # not connected
  L298N1 = L298N DC motor driver
  R3 = Rotary Potentiometer (Small) [maximum_resistance=100kΩ package=THT]  # not connected
  L298N2 = L298N DC motor driver  # not connected
  M1 = DC Motor
  R4 = Rotary Potentiometer (Small) [maximum_resistance=100kΩ package=THT]  # not connected
  M2 = DC Motor  # not connected
  R5 = Rotary Potentiometer (Small) [maximum_resistance=100kΩ package=THT]  # not connected
  M3 = DC Motor  # not connected
  R6 = Rotary Potentiometer (Small) [maximum_resistance=100kΩ package=THT]  # not connected
  M4 = DC Motor

nets:
  N1: L298N1.OUT1, M4.pin_2
  N2: L298N1.OUT2, M4.pin_1
  N3: L298N1.OUT3, M1.pin_2
  N4: L298N1.OUT4, M1.pin_1
  N5: L298N1.5V#9, L298N1.ENA
  N6: L298N1.5V#10, L298N1.ENB

custom parts:
  L298N DC motor driver: 2x DC motor driver with 78M05 positive voltage regulator (7..35 V) L298N: max 46 V, 2 A Set 5 V Enable jumper to enable 5 V regultor (needed for the L298N) and +5 V output at screw terminal or supply external +5 V at screw terminal Set ENA and/or ENB to +5 V to enable motor permanently or supply ENA and/or ENB with PWM signal IN1 and IN2 set rotation directory for motor A (OUT1/OUT2) IN2 and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
